// Logisim project DynamicConditions.circ as structural Verilog: 3 circuits, main circuit main
module main (
  input  in_1,
  input  in_2,
  output out_3,
  output [7:0] out_4
);

  wire clock_1_out;

  _1G3157 u_1g3157_1 (.O(out_3), .Y0(1'b0), .Y1(1'b1), .S(in_1));  // open: Sout
  Clock clock_1 (.out(clock_1_out));
  DecayingCounter decayingcounter_1 (.recharge(in_2), .clk(clock_1_out), .level(out_4));
endmodule

module _1G3157 (
  input  S,
  input  Y0,
  input  Y1,
  output Sout,
  output O
);

  Pull_Resistor pull_resistor_1 (.node(S));
  Multiplexer #(.disabled("Z"), .enable("false")) multiplexer_1 (.in0(Y0), .in1(Y1), .out(O), .sel(S));

  assign Sout = S;
endmodule

module DecayingCounter (
  input  recharge,
  input  clk,
  output [7:0] level
);

  wire comparator_1_gt, comparator_2_gt, comparator_3_lt;
  wire [7:0] adder_1_out, multiplexer_1_out, multiplexer_2_out, multiplexer_3_out, multiplexer_4_out;

  Adder adder_1 (.a(level), .b(multiplexer_1_out), .out(adder_1_out));  // open: cin, cout
  Multiplexer #(.enable("false"), .width(8)) multiplexer_1 (
    .in0(multiplexer_3_out), .in1(multiplexer_4_out), .out(multiplexer_1_out), .sel(recharge));
  Register register_1 (.D(adder_1_out), .Q(level), .clk(clk));  // open: en, clr
  Comparator #(.mode("unsigned")) comparator_1 (.a(level), .b(8'h40), .gt(comparator_1_gt));  // open: eq, lt
  Comparator #(.mode("unsigned")) comparator_2 (.a(level), .b({8{1'b0}}), .gt(comparator_2_gt));  // open: eq, lt
  Multiplexer #(.enable("false"), .width(8)) multiplexer_2 (
    .in0({8{1'b0}}), .in1({8{1'b1}}), .out(multiplexer_2_out), .sel(comparator_2_gt));
  Comparator #(.mode("unsigned")) comparator_3 (.a(level), .b({8{1'b1}}), .lt(comparator_3_lt));  // open: gt, eq
  Multiplexer #(.enable("false"), .width(8)) multiplexer_3 (
    .in0(multiplexer_2_out), .in1(8'hfe), .out(multiplexer_3_out), .sel(comparator_1_gt));
  Multiplexer #(.enable("false"), .width(8)) multiplexer_4 (
    .in0({8{1'b0}}), .in1(8'h1), .out(multiplexer_4_out), .sel(comparator_3_lt));
  LED #(.active("false")) led_1 (.in(comparator_3_lt));
endmodule
