// Logisim project IdealRelay.circ as structural Verilog: 2 circuits, main circuit main
module main (
  input  in_1,
  output out_2
);

  _1G3157 u_1g3157_1 (.O(out_2), .Y0(1'b0), .Y1(1'b1), .S(in_1));  // open: out_4
endmodule

module _1G3157 (
  input  S,
  input  Y0,
  input  Y1,
  output out_4,
  output O
);

  Pull_Resistor pull_resistor_1 (.node(S));
  Multiplexer #(.disabled("Z"), .enable("false")) multiplexer_1 (.in0(Y0), .in1(Y1), .out(O), .sel(S));
  LED led_1 (.in(S));

  assign out_4 = S;
endmodule
